// Logisim project RodrigoFerrazSouza_BIP.circ as structural Verilog: 13 circuits, main circuit main
module main (
);

  wire Caminho_de_Controle_en_ram, Caminho_de_Controle_en_rom, Caminho_de_Controle_sel_op2,
       Caminho_de_Controle_sel_ula, Caminho_de_Controle_wr_acc, Caminho_de_Controle_wr_ram, Clock_out,
       not_1_out, Reset_out;
  wire [1:0] Caminho_de_Controle_sel_op1;
  wire [3:0] caminho_de_dados_1_abcd__opcode;
  wire [11:0] Caminho_de_Controle_address_rom, caminho_de_dados_1_address_ram;
  wire [15:0] caminho_de_dados_1_din_ram, controlled_buffer_1_out, rom_1_data;

  Clock Clock (.out(Clock_out));
  Button Reset (.out(Reset_out));
  Caminho_de_Controle Caminho_de_Controle (
    .ABCD__OPCODE(caminho_de_dados_1_abcd__opcode), .Clock(Clock_out), .Reset(Reset_out),
    .ADDRESS_ROM(Caminho_de_Controle_address_rom), .EN_RAM(Caminho_de_Controle_en_ram),
    .WR_RAM(Caminho_de_Controle_wr_ram), .EN_ROM(Caminho_de_Controle_en_rom),
    .WR_ACC(Caminho_de_Controle_wr_acc), .SEL_OP1(Caminho_de_Controle_sel_op1),
    .SEL_OP2(Caminho_de_Controle_sel_op2), .SEL_ULA(Caminho_de_Controle_sel_ula));
  // Probe on caminho_de_dados_1_abcd__opcode
  // Probe on caminho_de_dados_1_din_ram
  Caminho_de_Dados caminho_de_dados_1 (
    .WR_ACC(Caminho_de_Controle_wr_acc), .SEL_OP1(Caminho_de_Controle_sel_op1),
    .SEL_OP2(Caminho_de_Controle_sel_op2), .SEL_ULA(Caminho_de_Controle_sel_ula), .DOUT_ROM(rom_1_data),
    .DOUT_RAM(controlled_buffer_1_out), .Clock(Clock_out), .ABCD__OPCODE(caminho_de_dados_1_abcd__opcode),
    .ADDRESS_RAM(caminho_de_dados_1_address_ram), .DIN_RAM(caminho_de_dados_1_din_ram), .RESET(Reset_out));
  assign controlled_buffer_1_out = not_1_out ? caminho_de_dados_1_din_ram : 16'bz;  // Controlled_Buffer controlled_buffer_1
  // Probe on Caminho_de_Controle_address_rom
  not not_1 (not_1_out, Caminho_de_Controle_wr_ram);
  // Probe on rom_1_data
  ROM #(.addrWidth(12), .dataWidth(16)) rom_1 (
    .addr(Caminho_de_Controle_address_rom), .data(rom_1_data), .sel(Caminho_de_Controle_en_rom));
  RAM #(.addrWidth(12), .dataWidth(16)) ram_1 (
    .addr(caminho_de_dados_1_address_ram), .data(controlled_buffer_1_out), .sel(Caminho_de_Controle_en_ram),
    .clk(Clock_out), .ld(Caminho_de_Controle_wr_ram), .clr(Reset_out));
  // Probe on controlled_buffer_1_out

  // Notes on the sheet:
  //   contents of rom_1 (hex, n*v repeats v):
  //   3013 1000 300a 1001 3023 1002 303f 1003 2000 4000 1004 6001 1004 4002 4002 4003 1004
endmodule

module Caminho_de_Controle (
  input  [3:0] ABCD__OPCODE,
  input  Clock,
  input  Reset,
  output [11:0] ADDRESS_ROM,
  output EN_RAM,
  output WR_RAM,
  output EN_ROM,
  output WR_ACC,
  output [1:0] SEL_OP1,
  output SEL_OP2,
  output SEL_ULA
);

  wire Logica_Controle_en_pc;

  Logica_de_Controle Logica_Controle (
    .A(ABCD__OPCODE[3]), .B(ABCD__OPCODE[2]), .C(ABCD__OPCODE[1]), .D(ABCD__OPCODE[0]),
    .EN_PC(Logica_Controle_en_pc), .EN_RAM(EN_RAM), .WR_RAM(WR_RAM), .EN_ROM(EN_ROM), .WR_ACC(WR_ACC),
    .SEL_OP1(SEL_OP1), .SEL_OP2(SEL_OP2), .SEL_ULA(SEL_ULA));
  // Probe on Logica_Controle_en_pc
  Address_Counter CamCont (.EN_PC(Logica_Controle_en_pc), .Clock(Clock), .Reset(Reset), .out_4(ADDRESS_ROM));
endmodule

module Address_Counter (
  input  EN_PC,
  input  Clock,
  input  Reset,
  output [11:0] out_4
);

  wire [11:0] adder_1_out;

  Adder #(.width(12)) adder_1 (.a(out_4), .b(12'h1), .out(adder_1_out));  // open: cin, cout
  Register #(.width(12)) PC (.D(adder_1_out), .en(EN_PC), .Q(out_4), .clk(Clock), .clr(Reset));
endmodule

module Logica_de_Controle (
  input  A,
  input  B,
  input  C,
  input  D,
  output EN_PC,
  output EN_RAM,
  output WR_RAM,
  output EN_ROM,
  output WR_ACC,
  output [1:0] SEL_OP1,
  output SEL_OP2,
  output SEL_ULA
);

  or or_1 (WR_ACC, B, C);
  SEL_OP2 sel_op2_1 (.B(B), .C(C), .D(D), .S(SEL_OP2));
  EN_PC en_pc_1 (.B(B), .C(C), .D(D), .SAIDA(EN_PC));
  EN_RAM en_ram_1 (.B(B), .C(C), .D(D), .S(EN_RAM));
  WR_RAM wr_ram_1 (.B(B), .C(C), .D(D), .SAIDA(WR_RAM));
  OP1 op1_1 (.B(B), .C(C), .D(D), .SAIDA(SEL_OP1));
  and and_1 (SEL_ULA, B, C);

  assign EN_ROM = 1'b1;
endmodule

module EN_PC (
  input  B,
  input  C,
  input  D,
  output SAIDA
);

  or or_1 (SAIDA, B, C, D);
endmodule

module WR_RAM (
  input  B,
  input  C,
  input  D,
  output SAIDA
);

  wire not_1_out, not_2_out;

  not not_1 (not_1_out, B);
  not not_2 (not_2_out, C);
  nand nand_1 (SAIDA, not_1_out, not_2_out, D);
endmodule

module OP1 (
  input  B,
  input  C,
  input  D,
  output [1:0] SAIDA
);

  wire not_1_out;

  not not_1 (not_1_out, B);
  and and_1 (SAIDA[0], not_1_out, C, D);

  assign SAIDA[1] = B;
endmodule

module SEL_OP2 (
  input  B,
  input  C,
  input  D,
  output S
);

  wire and_1_out, and_2_out;

  and and_1 (and_1_out, B, D);
  and and_2 (and_2_out, C, D);
  or or_1 (S, and_1_out, and_2_out);
endmodule

module EN_RAM (
  input  B,
  input  C,
  input  D,
  output S
);

  wire and_1_out, and_2_out, and_3_out, not_1_out, not_2_out, not_3_out;

  not not_1 (not_1_out, D);
  not not_2 (not_2_out, C);
  not not_3 (not_3_out, B);
  and and_1 (and_1_out, B, not_1_out);
  and and_2 (and_2_out, C, not_1_out);
  and and_3 (and_3_out, D, not_2_out, not_3_out);
  or or_1 (S, and_1_out, and_2_out, and_3_out);
endmodule

module Caminho_de_Dados (
  input  WR_ACC,
  input  [1:0] SEL_OP1,
  input  SEL_OP2,
  input  SEL_ULA,
  input  [15:0] DOUT_ROM,
  input  [15:0] DOUT_RAM,
  input  Clock,
  input  RESET,
  output [3:0] ABCD__OPCODE,
  output [11:0] ADDRESS_RAM,
  output [15:0] DIN_RAM
);

  wire [15:0] ALU_saida, bit_extender_1_out, multiplexer_1_out, multiplexer_2_out;

  ALU ALU (.SEL_ULA(SEL_ULA), .B(multiplexer_1_out), .A(DIN_RAM), .Saida(ALU_saida));
  Multiplexer #(.width(16), .enable("false")) multiplexer_1 (
    .in0(DOUT_RAM), .in1(bit_extender_1_out), .out(multiplexer_1_out), .sel(SEL_OP2));
  Instruction_Register IR (.DOUT_ROM(DOUT_ROM), .Clock(Clock), .ABCD__OPCODE(ABCD__OPCODE), .ADDRES_RAM(ADDRESS_RAM));
  assign bit_extender_1_out = {{4{1'b0}}, ADDRESS_RAM};  // Bit_Extender bit_extender_1
  Multiplexer #(.select(2), .width(16), .enable("false")) multiplexer_2 (
    .in0(DOUT_RAM), .in1(bit_extender_1_out), .in2(ALU_saida), .in3(ALU_saida), .out(multiplexer_2_out),
    .sel(SEL_OP1));
  Acumulador ACC (.ACC_IN(multiplexer_2_out), .CLOCK(Clock), .WR_ACC(WR_ACC), .RESET(RESET), .ACC_OUT(DIN_RAM));
  // Probe on DIN_RAM
endmodule

module ALU (
  input  [15:0] B,
  input  [15:0] A,
  input  SEL_ULA,
  output [15:0] Saida
);

  wire [15:0] adder_1_out, subtractor_1_out;

  Adder #(.width(16)) adder_1 (.a(A), .b(B), .out(adder_1_out));  // open: cin, cout
  Subtractor #(.width(16)) subtractor_1 (.a(A), .b(B), .out(subtractor_1_out));  // open: bin, bout
  Multiplexer #(.width(16), .enable("false")) multiplexer_1 (
    .in0(adder_1_out), .in1(subtractor_1_out), .out(Saida), .sel(SEL_ULA));
endmodule

module Instruction_Register (
  input  [15:0] DOUT_ROM,
  input  Clock,
  output [3:0] ABCD__OPCODE,
  output [11:0] ADDRES_RAM
);


  assign ABCD__OPCODE = DOUT_ROM[15:12];
  assign ADDRES_RAM = DOUT_ROM[11:0];
endmodule

module Acumulador (
  input  [15:0] ACC_IN,
  input  CLOCK,
  input  WR_ACC,
  input  RESET,
  output [15:0] ACC_OUT
);

  Register #(.width(16)) register_1 (.D(ACC_IN), .en(WR_ACC), .Q(ACC_OUT), .clk(CLOCK), .clr(RESET));
endmodule
